# Fritzing sketch Ethernet_W5500+LED (saved by Fritzing 0.9.3b)

parts:
  Componente1 = Arduino Uno (Rev3)
  W5500_Module2 = W5500 Ethernet module [package="DIP (Dual Inline) [THT]"]
  LED1 = LEDs [package=led10mm]

nets:
  N1: Componente1.D10_PWM/SS, W5500_Module2.SCS
  N2: Componente1.D11_PWM/MOSI, W5500_Module2.MOSI
  N3: Componente1.D12/MISO, W5500_Module2.MISO
  N4: Componente1.D13/SCK, W5500_Module2.SCLK
  GND: Componente1.GND, W5500_Module2.GND
  N5: Componente1.D2, W5500_Module2.INT
  N6: Componente1.D7, LED1.A
  3V3: Componente1.3V3, W5500_Module2.3.3V

custom parts:
  W5500 Ethernet module: W5500 based SPI Ethernet module for Arduino, etc.
